# Fritzing sketch Project 2 Schematic (saved by Fritzing 0.9.3b)
breadboards: 3

parts:
  U1 = LM124-324 Quad Opamp [package="DIP (Dual Inline)"]
  U2 = LM124-324 Quad Opamp [package="DIP (Dual Inline)"]
  U3 = LM124-324 Quad Opamp [package="DIP (Dual Inline)"]
  U4 = LM124-324 Quad Opamp [package="DIP (Dual Inline)"]
  R1 = Resistor [tolerance=±5% resistance=1k package=THT]
  R2 = Resistor [tolerance=±5% resistance=1k package=THT]
  R3 = Resistor [tolerance=±5% resistance=1k package=THT]
  R4 = Resistor [tolerance=±5% resistance=1k package=THT]
  R5 = Resistor [tolerance=±5% resistance=1k package=THT]
  R6 = Resistor [tolerance=±5% resistance=1k package=THT]
  R7 = Resistor [tolerance=±5% resistance=1k package=THT]
  R8 = Resistor [tolerance=±5% resistance=1k package=THT]
  R9 = Resistor [tolerance=±5% resistance=1k package=THT]
  R10 = Resistor [tolerance=±5% resistance=1k package=THT]
  Part2 = Arduino Mega 2560 (Rev3)
  R11 = Resistor [tolerance=±5% resistance=1k package=THT]
  R12 = Resistor [tolerance=±5% resistance=1k package=THT]
  R13 = Resistor [tolerance=±5% resistance=1k package=THT]
  R14 = Resistor [tolerance=±5% resistance=1k package=THT]
  R15 = Resistor [tolerance=±5% resistance=1k package=THT]
  R16 = Resistor [tolerance=±5% resistance=1k package=THT]
  LCD1 = LCD screen
  R18 = Resistor [tolerance=±5% resistance=10k package="0805 [SMD]"]
  R19 = Trimmer Potentiometer [maximum_resistance=10kΩ package=THT]

nets:
  N1: U1.1OUT, Part2.D8_PWM
  N2: U1.1IN-, R3.Pin_1, R6.Pin_0
  N3: U1.1IN+, U1.2IN+, U1.3IN+, U1.4IN+, U2.1IN+, U2.2IN+, U2.3IN+, U2.4IN+, U3.1IN+, U3.2IN+, U3.3IN+, U3.4IN+, U4.1IN+, U4.2IN+, U4.3IN+, U4.4IN+
  N4: U1.VCC+, U2.VCC+, U3.VCC+, U4.VCC+, Part2.5V
  N5: U1.2IN-, R1.Pin_1, R3.Pin_0
  N6: U1.2OUT, Part2.D9_PWM
  N7: U1.3OUT, Part2.D10_PWM
  N8: U1.3IN-, R1.Pin_0, R11.Pin_1
  N9: U1.VCC-, U2.VCC-, U3.VCC-, U4.VCC-, Part2.GND
  N10: U1.4IN-, R11.Pin_0, R12.Pin_1
  N11: U1.4OUT, Part2.D11_PWM
  N12: U2.1OUT, Part2.D4_PWM
  N13: U2.1IN-, R5.Pin_0, R8.Pin_1
  N14: U2.2IN-, R8.Pin_0, R10.Pin_1
  N15: U2.2OUT, Part2.D5_PWM
  N16: U2.3OUT, Part2.D6_PWM
  N17: U2.3IN-, R9.Pin_1, R10.Pin_0
  N18: U2.4IN-, R6.Pin_1, R9.Pin_0
  N19: U2.4OUT, Part2.D7_PWM
  N20: U3.1OUT, Part2.D12_PWM
  N21: U3.1IN-, R12.Pin_0, R13.Pin_1
  N22: U3.2IN-, R13.Pin_0, R14.Pin_1
  N23: U3.2OUT, Part2.D13_PWM
  N24: U3.3OUT, Part2.D14/TX3
  N25: U3.3IN-, R14.Pin_0, R15.Pin_0
  N26: U3.4IN-, R15.Pin_1, R16.Pin_0
  N27: U3.4OUT, Part2.D15/RX3
  N28: U4.1OUT, Part2.D0_RX0
  N29: U4.1IN-, R2.Pin_1
  N30: U4.2IN-, R2.Pin_0, R4.Pin_1
  N31: U4.2OUT, Part2.D1_TX0
  N32: U4.3OUT, Part2.D2_PWM
  N33: U4.3IN-, R4.Pin_0, R7.Pin_1
  N34: U4.4IN-, R5.Pin_1, R7.Pin_0
  N35: U4.4OUT, Part2.D3_PWM
  N36: Part2.D28, LCD1.DB7
  N37: Part2.D29, LCD1.DB6
  N38: Part2.D30, LCD1.DB5
  N39: Part2.D31, LCD1.DB4
  N40: Part2.D32, LCD1.DB0
  N41: Part2.D33, LCD1.R/W
  N42: LCD1.VSS, LCD1.E, LCD1.LED-, R19.leg1
  N43: LCD1.VDD, R18.Pin_0, R19.leg2
  N44: LCD1.V0, R19.wiper
  N45: LCD1.LED+, R18.Pin_1

// code stored in the sketch: proj2.ino
#include <LiquidCrystal.h>
#define VCC 12

//array to hold our comparators
const int comparators[] = {0, 1, 2, 3, 4, 5, 6, 7, 8, 9, 10, 11, 12, 13, 14, 15};
// Constant integers for 4 7-segment display
const int pinA = 16, pinB = 17, pinC = 18, pinD = 19,
          pinE = 20, pinF = 21, pinG = 22, pinDec = 23, D1 = 24,
          D2 = 25, D3 = 26, D4 = 27;
// LCD Constants
const int rs = 33, en = 32, d4 = 31, d5 = 30, d6 = 29, d7 = 28;
const double VOLTAGE_STEP = 0.75;

LiquidCrystal lcd(rs, en, d4, d5, d6, d7);
String outVoltage;

void sevenSegmentHelper(char digit, int index);
void sevenSegmentNumbers(char digit);
double comparatorRead();

void setup()
{
  //initialize comparator pins as inputs
  for (int index = 0; index < 16; index++)
  {
    pinMode(comparators[index], INPUT);
  }
  pinMode(pinA, OUTPUT);
  pinMode(pinB, OUTPUT);
  pinMode(pinC, OUTPUT);
  pinMode(pinD, OUTPUT);
  pinMode(pinE, OUTPUT);
  pinMode(pinF, OUTPUT);
  pinMode(pinG, OUTPUT);
  pinMode(pinDec, OUTPUT);
  pinMode(D1, OUTPUT);
  pinMode(D2, OUTPUT);
  pinMode(D3, OUTPUT);
  pinMode(D4, OUTPUT);
  lcd.begin(16, 2);
  Serial.begin(9600);

}

void loop()
{
  int index;
  char voltageChar;

  // Get the whole number voltage
  outVoltage = (String)comparatorRead();

  // Adds a 0 to the front of the number if not 10, 11, or 12
  if (outVoltage.charAt(0) != '1' && outVoltage.charAt(1) == ".")
  {
    outVoltage = "0" + outVoltage;
  }

  // Iterate through outVoltage and use seven seg helpers
  for (index = 0; index < 4; index++)
  {
    voltageChar = outVoltage.charAt(index);
    if (voltageChar != '.')
    {
      sevenSegmentHelper(voltageChar, index);
    }
  }

  Serial.println("Voltage: " + outVoltage);
  lcd.print("Voltage: " + outVoltage);
}

double comparatorRead()
{
  int index;
  double calculatedVoltage;
  for (index = 15; index >= 0 ; index--)
  {
    if (digitalRead(comparators[index]) == HIGH)
    {
      calculatedVoltage = (index + 1) * VOLTAGE_STEP;
      return calculatedVoltage;
    }
  }
  return 0;
}

void sevenSegmentHelper(char digit, int index)
{
  switch (index)
  {
    // If first digit
    case 0:
      digitalWrite(D1, LOW);
      digitalWrite(D2, HIGH);
      digitalWrite(D3, HIGH);
      digitalWrite(D4, HIGH);
      digitalWrite(pinDec, LOW);
      sevenSegmentNumbers(digit);
      break;

    // If second digit
    case 1:
      digitalWrite(D1, HIGH);
      digitalWrite(D2, LOW);
      digitalWrite(D3, HIGH);
      digitalWrite(D4, HIGH);
      digitalWrite(pinDec, HIGH);
      sevenSegmentNumbers(digit);
      break;

    // If third digit
    case 2:
      digitalWrite(D1, HIGH);
      digitalWrite(D2, HIGH);
      digitalWrite(D3, LOW);
      digitalWrite(D4, HIGH);
      digitalWrite(pinDec, LOW);
      sevenSegmentNumbers(digit);
      break;

    // If fourth digit
    case 3:
      digitalWrite(D1, HIGH);
      digitalWrite(D2, HIGH);
      digitalWrite(D3, HIGH);
      digitalWrite(D4, LOW);
      digitalWrite(pinDec, LOW);
      sevenSegmentNumbers(digit);
      break;
  }
}

void sevenSegmentNumbers(char digit)
{
  switch (digit)
  {
    // if digit is 0
    case '0':
      digitalWrite(pinA, HIGH);
      digitalWrite(pinB, HIGH);
      digitalWrite(pinC, HIGH);
      digitalWrite(pinD, HIGH);
      digitalWrite(pinE, HIGH);
      digitalWrite(pinF, HIGH);
      digitalWrite(pinG, LOW);
      delay(1);
      break;

    // if digit is 1
    case '1':
      digitalWrite(pinA, LOW);
      digitalWrite(pinB, HIGH);
      digitalWrite(pinC, HIGH);
      digitalWrite(pinD, LOW);
      digitalWrite(pinE, LOW);
      digitalWrite(pinF, LOW);
      digitalWrite(pinG, LOW);
      delay(1);
      break;

    // if digit is 2
    case '2':
      digitalWrite(pinA, HIGH);
      digitalWrite(pinB, HIGH);
      digitalWrite(pinC, LOW);
      digitalWrite(pinD, HIGH);
      digitalWrite(pinE, HIGH);
      digitalWrite(pinF, LOW);
      digitalWrite(pinG, HIGH);
      delay(1);
      break;

    // if digit is 3
    case '3':
      digitalWrite(pinA, HIGH);
      digitalWrite(pinB, HIGH);
      digitalWrite(pinC, HIGH);
      digitalWrite(pinD, HIGH);
      digitalWrite(pinE, LOW);
      digitalWrite(pinF, LOW);
      digitalWrite(pinG, HIGH);
      delay(1);
      break;

    // if digit is 4
    case '4':
      digitalWrite(pinA, LOW);
      digitalWrite(pinB, HIGH);
      digitalWrite(pinC, HIGH);
      digitalWrite(pinD, LOW);
      digitalWrite(pinE, LOW);
      digitalWrite(pinF, HIGH);
      digitalWrite(pinG, HIGH);
      delay(1);
      break;

    // if digit is 5
    case '5':
      digitalWrite(pinA, HIGH);
      digitalWrite(pinB, LOW);
      digitalWrite(pinC, HIGH);
      digitalWrite(pinD, HIGH);
      digitalWrite(pinE, LOW);
      digitalWrite(pinF, HIGH);
      digitalWrite(pinG, HIGH);
      delay(1);
      break;

    // if digit is 6
    case '6':
      digitalWrite(pinA, HIGH);
      digitalWrite(pinB, LOW);
      digitalWrite(pinC, HIGH);
      digitalWrite(pinD, HIGH);
      digitalWrite(pinE, HIGH);
      digitalWrite(pinF, HIGH);
      digitalWrite(pinG, HIGH);
      delay(1);
      break;

    // if digit is 7
    case '7':
      digitalWrite(pinA, HIGH);
      digitalWrite(pinB, HIGH);
      digitalWrite(pinC, HIGH);
      digitalWrite(pinD, LOW);
      digitalWrite(pinE, LOW);
      digitalWrite(pinF, LOW);
      digitalWrite(pinG, LOW);
      delay(1);
      break;

    // if digit is 8
    case '8':
      digitalWrite(pinA, HIGH);
      digitalWrite(pinB, HIGH);
      digitalWrite(pinC, HIGH);
      digitalWrite(pinD, HIGH);
      digitalWrite(pinE, HIGH);
      digitalWrite(pinF, HIGH);
      digitalWrite(pinG, HIGH);
      delay(1);
      break;

    // if digit is 9
    case '9':
      digitalWrite(pinA, HIGH);
      digitalWrite(pinB, HIGH);
      digitalWrite(pinC, HIGH);
      digitalWrite(pinD, HIGH);
      digitalWrite(pinE, LOW);
      digitalWrite(pinF, HIGH);
      digitalWrite(pinG, HIGH);
      delay(1);
      break;
  }
}
